// Logisim project ALU_8_Bit.circ as structural Verilog: 6 circuits, main circuit main
module main (
  input  D,
  input  CLK,
  input  Reset,
  input  Load,
  input  D1,
  input  CLK1,
  input  Reset1,
  input  Reset2,
  input  Load2,
  input  CLK2,
  input  [7:0] D2,
  input  [7:0] D3,
  input  [7:0] D4,
  output Q,
  output not_Q,
  output Q1,
  output not_Q1,
  output [7:0] Q2,
  output [7:0] not_Q2,
  output [7:0] Q3,
  output Uebertrag
);

  D_Flipflop d_flipflop_1 (.D(D), .CLK(CLK), .Reset(Reset), .Q(Q), .not_Q(not_Q));
  Register_1_Bit register_1_bit_1 (.Load(Load), .D(D1), .CLK(CLK1), .Reset(Reset1), .Q(Q1), .Q_negiert(not_Q1));
  Register_8_Bit register_8_bit_1 (.Reset(Reset2), .LOAD(Load2), .CLK(CLK2), .D(D2), .Q(Q2), .Nicht_Q(not_Q2));
  Addierer_8_Bit addierer_8_bit_1 (.In1(D3), .In2(D4), .Summe(Q3), .Uebertrag(Uebertrag));
endmodule

module D_Flipflop (
  input  D,
  input  CLK,
  input  Reset,
  output Q,
  output not_Q
);

  wire and_1_out, and_2_out, nand_1_out, nand_2_out, nand_3_out, nand_4_out, nand_5_out, nand_6_out,
       not_1_out, not_2_out, not_3_out, not_4_out, not_5_out, or_1_out, or_2_out;

  not not_1 (not_1_out, CLK);
  not not_2 (not_2_out, D);
  not not_3 (not_3_out, CLK);
  nand nand_1 (nand_1_out, D, not_1_out);
  nand nand_2 (nand_2_out, not_2_out, not_3_out);
  or or_1 (or_1_out, nand_1_out, Reset);
  not not_4 (not_4_out, Reset);
  and and_1 (and_1_out, nand_2_out, not_4_out);
  nand nand_3 (nand_3_out, or_1_out, nand_4_out);
  nand nand_4 (nand_4_out, nand_3_out, and_1_out);
  nand nand_5 (nand_5_out, nand_3_out, CLK);
  nand nand_6 (nand_6_out, CLK, nand_4_out);
  or or_2 (or_2_out, nand_5_out, Reset);
  not not_5 (not_5_out, Reset);
  and and_2 (and_2_out, nand_6_out, not_5_out);
  nand nand_7 (Q, or_2_out, not_Q);
  nand nand_8 (not_Q, Q, and_2_out);

  // Notes on the sheet:
  //   M1
  //   M2
  //   Master_Q
  //   Master_Q_negiert
  //   S1
  //   S2
  //   Slave_Q
  //   Slave_Q_negiert
endmodule

module Register_1_Bit (
  input  Load,
  input  D,
  input  CLK,
  input  Reset,
  output Q,
  output Q_negiert
);

  wire and_1_out, and_2_out, not_1_out, not_2_out, or_1_out;

  not not_1 (not_1_out, Load);
  not not_2 (not_2_out, not_1_out);
  and and_1 (and_1_out, Q, not_1_out);
  and and_2 (and_2_out, D, not_2_out);
  or or_1 (or_1_out, and_1_out, and_2_out);
  D_Flipflop d_flipflop_1 (.D(or_1_out), .CLK(CLK), .Reset(Reset), .Q(Q), .not_Q(Q_negiert));

  // Notes on the sheet:
  //   D_2
  //   D_1
  //   D_fuer_Flipflop
endmodule

module Register_8_Bit (
  input  Reset,
  input  LOAD,
  input  CLK,
  input  [7:0] D,
  output [7:0] Q,
  output [7:0] Nicht_Q
);

  Register_1_Bit register_1_bit_1 (.Load(LOAD), .D(D[0]), .CLK(CLK), .Reset(Reset), .Q(Q[0]), .Q_negiert(Nicht_Q[0]));
  Register_1_Bit register_1_bit_2 (.Load(LOAD), .D(D[1]), .CLK(CLK), .Reset(Reset), .Q(Q[1]), .Q_negiert(Nicht_Q[1]));
  Register_1_Bit register_1_bit_3 (.Load(LOAD), .D(D[2]), .CLK(CLK), .Reset(Reset), .Q(Q[2]), .Q_negiert(Nicht_Q[2]));
  Register_1_Bit register_1_bit_4 (.Load(LOAD), .D(D[3]), .CLK(CLK), .Reset(Reset), .Q(Q[3]), .Q_negiert(Nicht_Q[3]));
  Register_1_Bit register_1_bit_5 (.Load(LOAD), .D(D[4]), .CLK(CLK), .Reset(Reset), .Q(Q[4]), .Q_negiert(Nicht_Q[4]));
  Register_1_Bit register_1_bit_6 (.Load(LOAD), .D(D[5]), .CLK(CLK), .Reset(Reset), .Q(Q[5]), .Q_negiert(Nicht_Q[5]));
  Register_1_Bit register_1_bit_7 (.Load(LOAD), .D(D[6]), .CLK(CLK), .Reset(Reset), .Q(Q[6]), .Q_negiert(Nicht_Q[6]));
  Register_1_Bit register_1_bit_8 (.Load(LOAD), .D(D[7]), .CLK(CLK), .Reset(Reset), .Q(Q[7]), .Q_negiert(Nicht_Q[7]));
endmodule

module Addierer_Komponente (
  input  UebetragIn,
  input  Summand1,
  input  Summand2,
  output Ergebnis,
  output UebertragOut
);

  wire and_1_out, and_2_out, xor_1_out;

  xor xor_1 (xor_1_out, Summand1, Summand2);
  and and_1 (and_1_out, Summand1, Summand2);
  xor xor_2 (Ergebnis, xor_1_out, UebetragIn);
  and and_2 (and_2_out, xor_1_out, UebetragIn);
  or or_1 (UebertragOut, and_2_out, and_1_out);
endmodule

module Addierer_8_Bit (
  input  [7:0] In1,
  input  [7:0] In2,
  output [7:0] Summe,
  output Uebertrag
);

  wire addierer_komponente_1_uebertragout, addierer_komponente_2_uebertragout,
       addierer_komponente_3_uebertragout, addierer_komponente_4_uebertragout,
       addierer_komponente_5_uebertragout, addierer_komponente_6_uebertragout, and_1_out;

  xor xor_1 (Summe[0], In1[0], In2[0]);
  and and_1 (and_1_out, In1[0], In2[0]);
  Addierer_Komponente addierer_komponente_1 (
    .UebetragIn(and_1_out), .Summand1(In1[1]), .Summand2(In2[1]), .Ergebnis(Summe[1]),
    .UebertragOut(addierer_komponente_1_uebertragout));
  Addierer_Komponente addierer_komponente_2 (
    .UebetragIn(addierer_komponente_1_uebertragout), .Summand1(In1[2]), .Summand2(In2[2]),
    .Ergebnis(Summe[2]), .UebertragOut(addierer_komponente_2_uebertragout));
  Addierer_Komponente addierer_komponente_3 (
    .UebetragIn(addierer_komponente_2_uebertragout), .Summand1(In1[3]), .Summand2(In2[3]),
    .Ergebnis(Summe[3]), .UebertragOut(addierer_komponente_3_uebertragout));
  Addierer_Komponente addierer_komponente_4 (
    .UebetragIn(addierer_komponente_3_uebertragout), .Summand1(In1[4]), .Summand2(In2[4]),
    .Ergebnis(Summe[4]), .UebertragOut(addierer_komponente_4_uebertragout));
  Addierer_Komponente addierer_komponente_5 (
    .UebetragIn(addierer_komponente_4_uebertragout), .Summand1(In1[5]), .Summand2(In2[5]),
    .Ergebnis(Summe[5]), .UebertragOut(addierer_komponente_5_uebertragout));
  Addierer_Komponente addierer_komponente_6 (
    .UebetragIn(addierer_komponente_5_uebertragout), .Summand1(In1[6]), .Summand2(In2[6]),
    .Ergebnis(Summe[6]), .UebertragOut(addierer_komponente_6_uebertragout));
  Addierer_Komponente addierer_komponente_7 (
    .UebetragIn(addierer_komponente_6_uebertragout), .Summand1(In1[7]), .Summand2(In2[7]),
    .Ergebnis(Summe[7]), .UebertragOut(Uebertrag));
endmodule
