// Logisim project ALU_8_Bit_Projekt.circ as structural Verilog: 36 circuits, main circuit main
module main (
  input  D,
  input  CLK1,
  input  async_Reset,
  input  sync_Reset,
  input  Load,
  input  D1,
  input  CLK2,
  input  async_Reset1,
  input  sync_Reset1,
  input  async_reset2,
  input  sync_Reset2,
  input  Load2,
  input  CLK3,
  input  [7:0] D2,
  input  [7:0] D3,
  input  [7:0] D4,
  input  A_S,
  input  [7:0] D5,
  input  [7:0] D6,
  input  [7:0] Daten1,
  input  D_SHR,
  input  D_SHL,
  input  [1:0] s,
  input  Enable,
  input  CLK4,
  input  async_reset3,
  input  sync_reset3,
  input  [7:0] Operand1,
  input  [7:0] Operand2,
  input  [7:0] Operand1_1,
  input  [7:0] Operand1_2,
  input  CLK,
  input  [7:0] Daten,
  input  [7:0] Operation,
  output Q,
  output not_Q,
  output Q1,
  output not_Q1,
  output [7:0] Q2,
  output [7:0] not_Q2,
  output [7:0] Q3,
  output Uebertrag,
  output [7:0] Q4,
  output Uebertrag2,
  output [7:0] Ausgang,
  output [7:0] Ergebnis,
  output [7:0] Ergebnis2,
  output [7:0] Akkumulatorwert
);

  D_Flipflop d_flipflop_1 (.D(D), .CLK(CLK1), .async_Reset(async_Reset), .sync_Reset(sync_Reset), .Q(Q), .not_Q(not_Q));
  Register_1_Bit register_1_bit_1 (
    .Load(Load), .D(D1), .CLK(CLK2), .async_Reset(async_Reset1), .sync_Reset(sync_Reset1), .Q(Q1),
    .Q_negiert(not_Q1));
  Register_8_Bit register_8_bit_1 (
    .async_Reset(async_reset2), .sync_reset(sync_Reset2), .LOAD(Load2), .CLK(CLK3), .D(D2), .Q(Q2),
    .Nicht_Q(not_Q2));
  Addierer_8_Bit addierer_8_bit_1 (.Summand_1(D3), .Summand_2(D4), .Summe(Q3), .Uebertrag(Uebertrag));
  Addierer_Subtrahierer_8_Bit addierer_subtrahierer_8_bit_1 (
    .A_S(A_S), .In1(D5), .In2(D6), .Summe(Q4), .Uebertrag(Uebertrag2));
  Schieberegister_8_Bit schieberegister_8_bit_1 (
    .Daten(Daten1), .D_SHR(D_SHR), .D_SHL(D_SHL), .s(s), .Enable(Enable), .CLK(CLK4),
    .async_Reset(async_reset3), .sync_Reset(sync_reset3), .Ausgang(Ausgang));
  AND_8_Bit and_8_bit_1 (.Operand_1(Operand1), .Operand_2(Operand2), .Ausgang(Ergebnis));
  OR_8_Bit or_8_bit_1 (.Operand1(Operand1_1), .Operand2(Operand1_2), .Ausgang(Ergebnis2));
  ALU_8_Bit alu_8_bit_1 (.CLK(CLK), .Daten(Daten), .Operation(Operation), .Akkumulatorwert(Akkumulatorwert));

  // Notes on the sheet:
  //   SHR --> s = 01
  //   SHL --> s = 10
  //   LOAD --> s = 11
endmodule

module ALU_8_Bit (
  input  CLK,
  input  [7:0] Daten,
  input  [7:0] Operation,
  output [7:0] Akkumulatorwert
);


  // Notes on the sheet:
  //   Hier findet später die eigentliche Implementierung der ALU statt.
endmodule

module D_Flipflop (
  input  D,
  input  CLK,
  input  async_Reset,
  input  sync_Reset,
  output Q,
  output not_Q
);

  wire and_1_out, and_2_out, and_3_out, nand_1_out, nand_2_out, nand_3_out, nand_4_out, nand_5_out,
       nand_6_out, not_1_out, not_2_out, not_3_out, not_4_out, not_5_out, not_6_out, or_1_out, or_2_out;

  not not_1 (not_1_out, sync_Reset);
  and and_1 (and_1_out, not_1_out, D);
  not not_2 (not_2_out, CLK);
  not not_3 (not_3_out, and_1_out);
  not not_4 (not_4_out, CLK);
  nand nand_1 (nand_1_out, not_3_out, not_4_out);
  nand nand_2 (nand_2_out, and_1_out, not_2_out);
  not not_5 (not_5_out, async_Reset);
  or or_1 (or_1_out, nand_2_out, async_Reset);
  and and_2 (and_2_out, nand_1_out, not_5_out);
  nand nand_3 (nand_3_out, or_1_out, nand_4_out);
  nand nand_4 (nand_4_out, nand_3_out, and_2_out);
  nand nand_5 (nand_5_out, nand_3_out, CLK);
  nand nand_6 (nand_6_out, CLK, nand_4_out);
  or or_2 (or_2_out, nand_5_out, async_Reset);
  not not_6 (not_6_out, async_Reset);
  and and_3 (and_3_out, nand_6_out, not_6_out);
  nand nand_7 (Q, or_2_out, not_Q);
  nand nand_8 (not_Q, Q, and_3_out);

  // Notes on the sheet:
  //   D_intern
  //   M1
  //   M2
  //   Master_Q
  //   Master_Q_negiert
  //   S1
  //   S2
  //   Slave_Q
  //   Slave_Q_negiert
endmodule

module Register_1_Bit (
  input  Load,
  input  D,
  input  CLK,
  input  async_Reset,
  input  sync_Reset,
  output Q,
  output Q_negiert
);

  wire and_1_out, and_2_out, not_1_out, not_2_out, or_1_out;

  not not_1 (not_1_out, Load);
  not not_2 (not_2_out, not_1_out);
  and and_1 (and_1_out, Q, not_1_out);
  and and_2 (and_2_out, D, not_2_out);
  or or_1 (or_1_out, and_1_out, and_2_out);
  D_Flipflop d_flipflop_1 (
    .D(or_1_out), .CLK(CLK), .async_Reset(async_Reset), .sync_Reset(sync_Reset), .Q(Q), .not_Q(Q_negiert));

  // Notes on the sheet:
  //   D_2
  //   D_1
  //   D_fuer_Flipflop
endmodule

module Register_8_Bit (
  input  async_Reset,
  input  sync_reset,
  input  LOAD,
  input  CLK,
  input  [7:0] D,
  output [7:0] Q,
  output [7:0] Nicht_Q
);

  Register_1_Bit register_1_bit_1 (
    .Load(LOAD), .D(D[0]), .CLK(CLK), .async_Reset(async_Reset), .sync_Reset(sync_reset), .Q(Q[0]),
    .Q_negiert(Nicht_Q[0]));
  Register_1_Bit register_1_bit_2 (
    .Load(LOAD), .D(D[1]), .CLK(CLK), .async_Reset(async_Reset), .sync_Reset(sync_reset), .Q(Q[1]),
    .Q_negiert(Nicht_Q[1]));
  Register_1_Bit register_1_bit_3 (
    .Load(LOAD), .D(D[2]), .CLK(CLK), .async_Reset(async_Reset), .sync_Reset(sync_reset), .Q(Q[2]),
    .Q_negiert(Nicht_Q[2]));
  Register_1_Bit register_1_bit_4 (
    .Load(LOAD), .D(D[3]), .CLK(CLK), .async_Reset(async_Reset), .sync_Reset(sync_reset), .Q(Q[3]),
    .Q_negiert(Nicht_Q[3]));
  Register_1_Bit register_1_bit_5 (
    .Load(LOAD), .D(D[4]), .CLK(CLK), .async_Reset(async_Reset), .sync_Reset(sync_reset), .Q(Q[4]),
    .Q_negiert(Nicht_Q[4]));
  Register_1_Bit register_1_bit_6 (
    .Load(LOAD), .D(D[5]), .CLK(CLK), .async_Reset(async_Reset), .sync_Reset(sync_reset), .Q(Q[5]),
    .Q_negiert(Nicht_Q[5]));
  Register_1_Bit register_1_bit_7 (
    .Load(LOAD), .D(D[6]), .CLK(CLK), .async_Reset(async_Reset), .sync_Reset(sync_reset), .Q(Q[6]),
    .Q_negiert(Nicht_Q[6]));
  Register_1_Bit register_1_bit_8 (
    .Load(LOAD), .D(D[7]), .CLK(CLK), .async_Reset(async_Reset), .sync_Reset(sync_reset), .Q(Q[7]),
    .Q_negiert(Nicht_Q[7]));
endmodule

module Schieberegister_8_Bit (
  input  [7:0] Daten,
  input  D_SHR,
  input  D_SHL,
  input  [1:0] s,
  input  Enable,
  input  CLK,
  input  async_Reset,
  input  sync_Reset,
  output [7:0] Ausgang
);

  wire MUX_0_out_6, MUX_1_out_6, MUX_2_out_6, MUX_3_out_6, MUX_4_out_6, MUX_5_out_6, MUX_6_out_6, MUX_7_out_6;

  MUX_1_Bit_4x1 MUX_7 (.D0(Ausgang[7]), .D1(D_SHR), .D2(Ausgang[6]), .D3(Daten[7]), .s(s), .out_6(MUX_7_out_6));
  Register_1_Bit Register_7 (
    .Load(Enable), .D(MUX_7_out_6), .CLK(CLK), .async_Reset(async_Reset), .sync_Reset(sync_Reset),
    .Q(Ausgang[7]));  // open: Q_negiert
  MUX_1_Bit_4x1 MUX_6 (.D0(Ausgang[6]), .D1(Ausgang[7]), .D2(Ausgang[5]), .D3(Daten[6]), .s(s), .out_6(MUX_6_out_6));
  Register_1_Bit Register_6 (
    .Load(Enable), .D(MUX_6_out_6), .CLK(CLK), .async_Reset(async_Reset), .sync_Reset(sync_Reset),
    .Q(Ausgang[6]));  // open: Q_negiert
  MUX_1_Bit_4x1 MUX_5 (.D0(Ausgang[5]), .D1(Ausgang[6]), .D2(Ausgang[4]), .D3(Daten[5]), .s(s), .out_6(MUX_5_out_6));
  Register_1_Bit Register_5 (
    .Load(Enable), .D(MUX_5_out_6), .CLK(CLK), .async_Reset(async_Reset), .sync_Reset(sync_Reset),
    .Q(Ausgang[5]));  // open: Q_negiert
  MUX_1_Bit_4x1 MUX_4 (.D0(Ausgang[4]), .D1(Ausgang[5]), .D2(Ausgang[3]), .D3(Daten[4]), .s(s), .out_6(MUX_4_out_6));
  Register_1_Bit Register_4 (
    .Load(Enable), .D(MUX_4_out_6), .CLK(CLK), .async_Reset(async_Reset), .sync_Reset(sync_Reset),
    .Q(Ausgang[4]));  // open: Q_negiert
  MUX_1_Bit_4x1 MUX_3 (.D0(Ausgang[3]), .D1(Ausgang[4]), .D2(Ausgang[2]), .D3(Daten[3]), .s(s), .out_6(MUX_3_out_6));
  Register_1_Bit Register_3 (
    .Load(Enable), .D(MUX_3_out_6), .CLK(CLK), .async_Reset(async_Reset), .sync_Reset(sync_Reset),
    .Q(Ausgang[3]));  // open: Q_negiert
  MUX_1_Bit_4x1 MUX_2 (.D0(Ausgang[2]), .D1(Ausgang[3]), .D2(Ausgang[1]), .D3(Daten[2]), .s(s), .out_6(MUX_2_out_6));
  Register_1_Bit Register_2 (
    .Load(Enable), .D(MUX_2_out_6), .CLK(CLK), .async_Reset(async_Reset), .sync_Reset(sync_Reset),
    .Q(Ausgang[2]));  // open: Q_negiert
  MUX_1_Bit_4x1 MUX_1 (.D0(Ausgang[1]), .D1(Ausgang[2]), .D2(Ausgang[0]), .D3(Daten[1]), .s(s), .out_6(MUX_1_out_6));
  Register_1_Bit Register_1 (
    .Load(Enable), .D(MUX_1_out_6), .CLK(CLK), .async_Reset(async_Reset), .sync_Reset(sync_Reset),
    .Q(Ausgang[1]));  // open: Q_negiert
  MUX_1_Bit_4x1 MUX_0 (.D0(Ausgang[0]), .D1(Ausgang[1]), .D2(D_SHL), .D3(Daten[0]), .s(s), .out_6(MUX_0_out_6));
  Register_1_Bit Register_0 (
    .Load(Enable), .D(MUX_0_out_6), .CLK(CLK), .async_Reset(async_Reset), .sync_Reset(sync_Reset),
    .Q(Ausgang[0]));  // open: Q_negiert
endmodule

module Addierer_Komponente (
  input  Uebetrag_In,
  input  Summand_1,
  input  Summand_2,
  output Ergebnis,
  output Uebertrag_Out
);

  wire and_1_out, and_2_out, xor_1_out;

  xor xor_1 (xor_1_out, Summand_1, Summand_2);
  and and_1 (and_1_out, Summand_1, Summand_2);
  xor xor_2 (Ergebnis, xor_1_out, Uebetrag_In);
  and and_2 (and_2_out, xor_1_out, Uebetrag_In);
  or or_1 (Uebertrag_Out, and_2_out, and_1_out);

  // Notes on the sheet:
  //   a
  //   b
  //   c
endmodule

module Addierer_8_Bit (
  input  [7:0] Summand_1,
  input  [7:0] Summand_2,
  output [7:0] Summe,
  output Uebertrag
);

  wire Addierer_Komponente_1_uebertrag_out, Addierer_Komponente_2_uebertrag_out,
       Addierer_Komponente_3_uebertrag_out, Addierer_Komponente_4_uebertrag_out,
       Addierer_Komponente_5_uebertrag_out, Addierer_Komponente_6_uebertrag_out, and_1_out;

  xor xor_1 (Summe[0], Summand_1[0], Summand_2[0]);
  and and_1 (and_1_out, Summand_1[0], Summand_2[0]);
  Addierer_Komponente Addierer_Komponente_1 (
    .Uebetrag_In(and_1_out), .Summand_1(Summand_1[1]), .Summand_2(Summand_2[1]), .Ergebnis(Summe[1]),
    .Uebertrag_Out(Addierer_Komponente_1_uebertrag_out));
  Addierer_Komponente Addierer_Komponente_2 (
    .Uebetrag_In(Addierer_Komponente_1_uebertrag_out), .Summand_1(Summand_1[2]), .Summand_2(Summand_2[2]),
    .Ergebnis(Summe[2]), .Uebertrag_Out(Addierer_Komponente_2_uebertrag_out));
  Addierer_Komponente Addierer_Komponente_3 (
    .Uebetrag_In(Addierer_Komponente_2_uebertrag_out), .Summand_1(Summand_1[3]), .Summand_2(Summand_2[3]),
    .Ergebnis(Summe[3]), .Uebertrag_Out(Addierer_Komponente_3_uebertrag_out));
  Addierer_Komponente Addierer_Komponente_4 (
    .Uebetrag_In(Addierer_Komponente_3_uebertrag_out), .Summand_1(Summand_1[4]), .Summand_2(Summand_2[4]),
    .Ergebnis(Summe[4]), .Uebertrag_Out(Addierer_Komponente_4_uebertrag_out));
  Addierer_Komponente Addierer_Komponente_5 (
    .Uebetrag_In(Addierer_Komponente_4_uebertrag_out), .Summand_1(Summand_1[5]), .Summand_2(Summand_2[5]),
    .Ergebnis(Summe[5]), .Uebertrag_Out(Addierer_Komponente_5_uebertrag_out));
  Addierer_Komponente Addierer_Komponente_6 (
    .Uebetrag_In(Addierer_Komponente_5_uebertrag_out), .Summand_1(Summand_1[6]), .Summand_2(Summand_2[6]),
    .Ergebnis(Summe[6]), .Uebertrag_Out(Addierer_Komponente_6_uebertrag_out));
  Addierer_Komponente Addierer_Komponente_7 (
    .Uebetrag_In(Addierer_Komponente_6_uebertrag_out), .Summand_1(Summand_1[7]), .Summand_2(Summand_2[7]),
    .Ergebnis(Summe[7]), .Uebertrag_Out(Uebertrag));

  // Notes on the sheet:
  //   a
endmodule

module MUX_1_Bit_2x1 (
  input  s,
  input  D0,
  input  D1,
  output y
);

  wire and_1_out, and_2_out, not_1_out;

  and and_1 (and_1_out, D0, not_1_out);
  not not_1 (not_1_out, s);
  and and_2 (and_2_out, D1, s);
  or or_1 (y, and_1_out, and_2_out);
endmodule

module MUX_1_Bit_4x1 (
  input  D0,
  input  D1,
  input  D2,
  input  D3,
  input  [1:0] s,
  output out_6
);

  wire MUX_1_y, MUX_2_y;

  MUX_1_Bit_2x1 MUX_1 (.s(s[0]), .D0(D0), .D1(D1), .y(MUX_1_y));
  MUX_1_Bit_2x1 MUX_2 (.s(s[0]), .D0(D2), .D1(D3), .y(MUX_2_y));
  MUX_1_Bit_2x1 MUX_3 (.s(s[1]), .D0(MUX_1_y), .D1(MUX_2_y), .y(out_6));
endmodule

module MUX_1_Bit_8x1 (
  input  D0,
  input  D1,
  input  D2,
  input  D3,
  input  D4,
  input  D5,
  input  D6,
  input  D7,
  input  [2:0] s,
  output out_10
);

  wire MUX_1_out_6, MUX_2_out_6;

  MUX_1_Bit_4x1 MUX_1 (.D0(D0), .D1(D1), .D2(D2), .D3(D3), .s(s[1:0]), .out_6(MUX_1_out_6));
  MUX_1_Bit_4x1 MUX_2 (.D0(D4), .D1(D5), .D2(D6), .D3(D7), .s(s[1:0]), .out_6(MUX_2_out_6));
  MUX_1_Bit_2x1 MUX_3 (.s(s[2]), .D0(MUX_1_out_6), .D1(MUX_2_out_6), .y(out_10));
endmodule

module MUX_1_Bit_16x1 (
  input  D0,
  input  D1,
  input  D2,
  input  D3,
  input  D4,
  input  D5,
  input  D6,
  input  D7,
  input  D8,
  input  D9,
  input  D10,
  input  D11,
  input  D12,
  input  D13,
  input  D14,
  input  D15,
  input  [3:0] in_17,
  output y
);

  wire MUX_1_out_10, MUX_2_out_10;

  MUX_1_Bit_8x1 MUX_1 (
    .D0(D0), .D1(D1), .D2(D2), .D3(D3), .D4(D4), .D5(D5), .D6(D6), .D7(D7), .s(in_17[2:0]),
    .out_10(MUX_1_out_10));
  MUX_1_Bit_8x1 MUX_2 (
    .D0(D8), .D1(D9), .D2(D10), .D3(D11), .D4(D12), .D5(D13), .D6(D14), .D7(D15), .s(in_17[2:0]),
    .out_10(MUX_2_out_10));
  MUX_1_Bit_2x1 MUX_3 (.s(in_17[3]), .D0(MUX_1_out_10), .D1(MUX_2_out_10), .y(y));
endmodule

module MUX_2_Bit_16x1 (
  input  [1:0] D0,
  input  [1:0] D1,
  input  [1:0] D2,
  input  [1:0] D3,
  input  [1:0] D4,
  input  [1:0] D5,
  input  [1:0] D6,
  input  [1:0] D7,
  input  [1:0] D8,
  input  [1:0] D9,
  input  [1:0] D10,
  input  [1:0] D11,
  input  [1:0] D12,
  input  [1:0] D13,
  input  [1:0] D14,
  input  [1:0] D15,
  input  [3:0] s,
  output [1:0] y
);

  MUX_1_Bit_16x1 mux_1_bit_16x1_1 (
    .D0(D0[0]), .D1(D1[0]), .D2(D2[0]), .D3(D3[0]), .D4(D4[0]), .D5(D5[0]), .D6(D6[0]), .D7(D7[0]),
    .D8(D8[0]), .D9(D9[0]), .D10(D10[0]), .D11(D11[0]), .D12(D12[0]), .D13(D13[0]), .D14(D14[0]),
    .D15(D15[0]), .in_17(s), .y(y[0]));
  MUX_1_Bit_16x1 mux_1_bit_16x1_2 (
    .D0(D0[1]), .D1(D1[1]), .D2(D2[1]), .D3(D3[1]), .D4(D4[1]), .D5(D5[1]), .D6(D6[1]), .D7(D7[1]),
    .D8(D8[1]), .D9(D9[1]), .D10(D10[1]), .D11(D11[1]), .D12(D12[1]), .D13(D13[1]), .D14(D14[1]),
    .D15(D15[1]), .in_17(s), .y(y[1]));
endmodule

module MUX_4_Bit_16x1 (
  input  [3:0] D0,
  input  [3:0] D1,
  input  [3:0] D2,
  input  [3:0] D3,
  input  [3:0] D4,
  input  [3:0] D5,
  input  [3:0] D6,
  input  [3:0] D7,
  input  [3:0] D8,
  input  [3:0] D9,
  input  [3:0] D10,
  input  [3:0] D11,
  input  [3:0] D12,
  input  [3:0] D13,
  input  [3:0] D14,
  input  [3:0] D15,
  input  [3:0] s,
  output [3:0] y
);

  MUX_2_Bit_16x1 mux_2_bit_16x1_1 (
    .D0(D0[1:0]), .D1(D1[1:0]), .D2(D2[1:0]), .D3(D3[1:0]), .D4(D4[1:0]), .D5(D5[1:0]), .D6(D6[1:0]),
    .D7(D7[1:0]), .D8(D8[1:0]), .D9(D9[1:0]), .D10(D10[1:0]), .D11(D11[1:0]), .D12(D12[1:0]), .D13(D13[1:0]),
    .D14(D14[1:0]), .D15(D15[1:0]), .s(s), .y(y[1:0]));
  MUX_2_Bit_16x1 mux_2_bit_16x1_2 (
    .D0(D0[3:2]), .D1(D1[3:2]), .D2(D2[3:2]), .D3(D3[3:2]), .D4(D4[3:2]), .D5(D5[3:2]), .D6(D6[3:2]),
    .D7(D7[3:2]), .D8(D8[3:2]), .D9(D9[3:2]), .D10(D10[3:2]), .D11(D11[3:2]), .D12(D12[3:2]), .D13(D13[3:2]),
    .D14(D14[3:2]), .D15(D15[3:2]), .s(s), .y(y[3:2]));
endmodule

module MUX_8_Bit_16x1 (
  input  [7:0] D0,
  input  [7:0] D1,
  input  [7:0] D2,
  input  [7:0] D3,
  input  [7:0] D4,
  input  [7:0] D5,
  input  [7:0] D6,
  input  [7:0] D7,
  input  [7:0] D8,
  input  [7:0] D9,
  input  [7:0] D10,
  input  [7:0] D11,
  input  [7:0] D12,
  input  [7:0] D13,
  input  [7:0] D14,
  input  [7:0] D15,
  input  [3:0] s,
  output [7:0] y
);

  MUX_4_Bit_16x1 mux_4_bit_16x1_1 (
    .D0(D0[3:0]), .D1(D1[3:0]), .D2(D2[3:0]), .D3(D3[3:0]), .D4(D4[3:0]), .D5(D5[3:0]), .D6(D6[3:0]),
    .D7(D7[3:0]), .D8(D8[3:0]), .D9(D9[3:0]), .D10(D10[3:0]), .D11(D11[3:0]), .D12(D12[3:0]), .D13(D13[3:0]),
    .D14(D14[3:0]), .D15(D15[3:0]), .s(s), .y(y[3:0]));
  MUX_4_Bit_16x1 mux_4_bit_16x1_2 (
    .D0(D0[7:4]), .D1(D1[7:4]), .D2(D2[7:4]), .D3(D3[7:4]), .D4(D4[7:4]), .D5(D5[7:4]), .D6(D6[7:4]),
    .D7(D7[7:4]), .D8(D8[7:4]), .D9(D9[7:4]), .D10(D10[7:4]), .D11(D11[7:4]), .D12(D12[7:4]), .D13(D13[7:4]),
    .D14(D14[7:4]), .D15(D15[7:4]), .s(s), .y(y[7:4]));
endmodule

module MUX_1_Bit_32x1 (
  input  D0,
  input  D1,
  input  D2,
  input  D3,
  input  D4,
  input  D5,
  input  D6,
  input  D7,
  input  D8,
  input  D9,
  input  D10,
  input  D11,
  input  D12,
  input  D13,
  input  D14,
  input  D15,
  input  D16,
  input  D17,
  input  D18,
  input  D19,
  input  D20,
  input  D21,
  input  D22,
  input  D23,
  input  D24,
  input  D25,
  input  D26,
  input  D27,
  input  D28,
  input  D29,
  input  D30,
  input  D31,
  input  [4:0] s,
  output out_34
);

  wire MUX_1_y, MUX_2_y;

  MUX_1_Bit_16x1 MUX_1 (
    .D0(D0), .D1(D1), .D2(D2), .D3(D3), .D4(D4), .D5(D5), .D6(D6), .D7(D7), .D8(D8), .D9(D9), .D10(D10),
    .D11(D11), .D12(D12), .D13(D13), .D14(D14), .D15(D15), .in_17(s[3:0]), .y(MUX_1_y));
  MUX_1_Bit_16x1 MUX_2 (
    .D0(D16), .D1(D17), .D2(D18), .D3(D19), .D4(D20), .D5(D21), .D6(D22), .D7(D23), .D8(D24), .D9(D25),
    .D10(D26), .D11(D27), .D12(D28), .D13(D29), .D14(D30), .D15(D31), .in_17(s[3:0]), .y(MUX_2_y));
  MUX_1_Bit_2x1 MUX_3 (.s(s[4]), .D0(MUX_1_y), .D1(MUX_2_y), .y(out_34));
endmodule

module MUX_2_Bit_32x1 (
  input  [1:0] D0,
  input  [1:0] D1,
  input  [1:0] D2,
  input  [1:0] D3,
  input  [1:0] D4,
  input  [1:0] D5,
  input  [1:0] D6,
  input  [1:0] D7,
  input  [1:0] D8,
  input  [1:0] D9,
  input  [1:0] D10,
  input  [1:0] D11,
  input  [1:0] D12,
  input  [1:0] D13,
  input  [1:0] D14,
  input  [1:0] D15,
  input  [1:0] D16,
  input  [1:0] D17,
  input  [1:0] D18,
  input  [1:0] D19,
  input  [1:0] D20,
  input  [1:0] D21,
  input  [1:0] D22,
  input  [1:0] D23,
  input  [1:0] D24,
  input  [1:0] D25,
  input  [1:0] D26,
  input  [1:0] D27,
  input  [1:0] D28,
  input  [1:0] D29,
  input  [1:0] D30,
  input  [1:0] D31,
  input  [4:0] s,
  output [1:0] y
);

  MUX_1_Bit_32x1 MUX_1 (
    .D0(D0[0]), .D1(D1[0]), .D2(D2[0]), .D3(D3[0]), .D4(D4[0]), .D5(D5[0]), .D6(D6[0]), .D7(D7[0]),
    .D8(D8[0]), .D9(D9[0]), .D10(D10[0]), .D11(D11[0]), .D12(D12[0]), .D13(D13[0]), .D14(D14[0]),
    .D15(D15[0]), .D16(D16[0]), .D17(D17[0]), .D18(D18[0]), .D19(D19[0]), .D20(D20[0]), .D21(D21[0]),
    .D22(D22[0]), .D23(D23[0]), .D24(D24[0]), .D25(D25[0]), .D26(D26[0]), .D27(D27[0]), .D28(D28[0]),
    .D29(D29[0]), .D30(D30[0]), .D31(D31[0]), .s(s), .out_34(y[0]));
  MUX_1_Bit_32x1 MUX_2 (
    .D0(D0[1]), .D1(D1[1]), .D2(D2[1]), .D3(D3[1]), .D4(D4[1]), .D5(D5[1]), .D6(D6[1]), .D7(D7[1]),
    .D8(D8[1]), .D9(D9[1]), .D10(D10[1]), .D11(D11[1]), .D12(D12[1]), .D13(D13[1]), .D14(D14[1]),
    .D15(D15[1]), .D16(D16[1]), .D17(D17[1]), .D18(D18[1]), .D19(D19[1]), .D20(D20[1]), .D21(D21[1]),
    .D22(D22[1]), .D23(D23[1]), .D24(D24[1]), .D25(D25[1]), .D26(D26[1]), .D27(D27[1]), .D28(D28[1]),
    .D29(D29[1]), .D30(D30[1]), .D31(D31[1]), .s(s), .out_34(y[1]));
endmodule

module MUX_4_Bit_32x1 (
  input  [3:0] D0,
  input  [3:0] D1,
  input  [3:0] D2,
  input  [3:0] D3,
  input  [3:0] D4,
  input  [3:0] D5,
  input  [3:0] D6,
  input  [3:0] D7,
  input  [3:0] D8,
  input  [3:0] D9,
  input  [3:0] D10,
  input  [3:0] D11,
  input  [3:0] D12,
  input  [3:0] D13,
  input  [3:0] D14,
  input  [3:0] D15,
  input  [3:0] D16,
  input  [3:0] D17,
  input  [3:0] D18,
  input  [3:0] D19,
  input  [3:0] D20,
  input  [3:0] D21,
  input  [3:0] D22,
  input  [3:0] D23,
  input  [3:0] D24,
  input  [3:0] D25,
  input  [3:0] D26,
  input  [3:0] D27,
  input  [3:0] D28,
  input  [3:0] D29,
  input  [3:0] D30,
  input  [3:0] D31,
  input  [4:0] s,
  output [3:0] y
);

  MUX_2_Bit_32x1 MUX_1 (
    .D0(D0[1:0]), .D1(D1[1:0]), .D2(D2[1:0]), .D3(D3[1:0]), .D4(D4[1:0]), .D5(D5[1:0]), .D6(D6[1:0]),
    .D7(D7[1:0]), .D8(D8[1:0]), .D9(D9[1:0]), .D10(D10[1:0]), .D11(D11[1:0]), .D12(D12[1:0]), .D13(D13[1:0]),
    .D14(D14[1:0]), .D15(D15[1:0]), .D16(D16[1:0]), .D17(D17[1:0]), .D18(D18[1:0]), .D19(D19[1:0]),
    .D20(D20[1:0]), .D21(D21[1:0]), .D22(D22[1:0]), .D23(D23[1:0]), .D24(D24[1:0]), .D25(D25[1:0]),
    .D26(D26[1:0]), .D27(D27[1:0]), .D28(D28[1:0]), .D29(D29[1:0]), .D30(D30[1:0]), .D31(D31[1:0]), .s(s),
    .y(y[1:0]));
  MUX_2_Bit_32x1 MUX_2 (
    .D0(D0[3:2]), .D1(D1[3:2]), .D2(D2[3:2]), .D3(D3[3:2]), .D4(D4[3:2]), .D5(D5[3:2]), .D6(D6[3:2]),
    .D7(D7[3:2]), .D8(D8[3:2]), .D9(D9[3:2]), .D10(D10[3:2]), .D11(D11[3:2]), .D12(D12[3:2]), .D13(D13[3:2]),
    .D14(D14[3:2]), .D15(D15[3:2]), .D16(D16[3:2]), .D17(D17[3:2]), .D18(D18[3:2]), .D19(D19[3:2]),
    .D20(D20[3:2]), .D21(D21[3:2]), .D22(D22[3:2]), .D23(D23[3:2]), .D24(D24[3:2]), .D25(D25[3:2]),
    .D26(D26[3:2]), .D27(D27[3:2]), .D28(D28[3:2]), .D29(D29[3:2]), .D30(D30[3:2]), .D31(D31[3:2]), .s(s),
    .y(y[3:2]));
endmodule

module MUX_8_Bit_32x1 (
  input  [7:0] D0,
  input  [7:0] D1,
  input  [7:0] D2,
  input  [7:0] D3,
  input  [7:0] D4,
  input  [7:0] D5,
  input  [7:0] D6,
  input  [7:0] D7,
  input  [7:0] D8,
  input  [7:0] D9,
  input  [7:0] D10,
  input  [7:0] D11,
  input  [7:0] D12,
  input  [7:0] D13,
  input  [7:0] D14,
  input  [7:0] D15,
  input  [7:0] D16,
  input  [7:0] D17,
  input  [7:0] D18,
  input  [7:0] D19,
  input  [7:0] D20,
  input  [7:0] D21,
  input  [7:0] D22,
  input  [7:0] D23,
  input  [7:0] D24,
  input  [7:0] D25,
  input  [7:0] D26,
  input  [7:0] D27,
  input  [7:0] D28,
  input  [7:0] D29,
  input  [7:0] D30,
  input  [7:0] D31,
  input  [4:0] s,
  output [7:0] y
);

  MUX_4_Bit_32x1 MUX_1 (
    .D0(D0[3:0]), .D1(D1[3:0]), .D2(D2[3:0]), .D3(D3[3:0]), .D4(D4[3:0]), .D5(D5[3:0]), .D6(D6[3:0]),
    .D7(D7[3:0]), .D8(D8[3:0]), .D9(D9[3:0]), .D10(D10[3:0]), .D11(D11[3:0]), .D12(D12[3:0]), .D13(D13[3:0]),
    .D14(D14[3:0]), .D15(D15[3:0]), .D16(D16[3:0]), .D17(D17[3:0]), .D18(D18[3:0]), .D19(D19[3:0]),
    .D20(D20[3:0]), .D21(D21[3:0]), .D22(D22[3:0]), .D23(D23[3:0]), .D24(D24[3:0]), .D25(D25[3:0]),
    .D26(D26[3:0]), .D27(D27[3:0]), .D28(D28[3:0]), .D29(D29[3:0]), .D30(D30[3:0]), .D31(D31[3:0]), .s(s),
    .y(y[3:0]));
  MUX_4_Bit_32x1 MUX_2 (
    .D0(D0[7:4]), .D1(D1[7:4]), .D2(D2[7:4]), .D3(D3[7:4]), .D4(D4[7:4]), .D5(D5[7:4]), .D6(D6[7:4]),
    .D7(D7[7:4]), .D8(D8[7:4]), .D9(D9[7:4]), .D10(D10[7:4]), .D11(D11[7:4]), .D12(D12[7:4]), .D13(D13[7:4]),
    .D14(D14[7:4]), .D15(D15[7:4]), .D16(D16[7:4]), .D17(D17[7:4]), .D18(D18[7:4]), .D19(D19[7:4]),
    .D20(D20[7:4]), .D21(D21[7:4]), .D22(D22[7:4]), .D23(D23[7:4]), .D24(D24[7:4]), .D25(D25[7:4]),
    .D26(D26[7:4]), .D27(D27[7:4]), .D28(D28[7:4]), .D29(D29[7:4]), .D30(D30[7:4]), .D31(D31[7:4]), .s(s),
    .y(y[7:4]));
endmodule

module MUX_16_Bit_32x1 (
  input  [15:0] D0,
  input  [15:0] D1,
  input  [15:0] D2,
  input  [15:0] D3,
  input  [15:0] D4,
  input  [15:0] D5,
  input  [15:0] D6,
  input  [15:0] D7,
  input  [15:0] D8,
  input  [15:0] D9,
  input  [15:0] D10,
  input  [15:0] D11,
  input  [15:0] D12,
  input  [15:0] D13,
  input  [15:0] D14,
  input  [15:0] D15,
  input  [15:0] D16,
  input  [15:0] D17,
  input  [15:0] D18,
  input  [15:0] D19,
  input  [15:0] D20,
  input  [15:0] D21,
  input  [15:0] D22,
  input  [15:0] D23,
  input  [15:0] D24,
  input  [15:0] D25,
  input  [15:0] D26,
  input  [15:0] D27,
  input  [15:0] D28,
  input  [15:0] D29,
  input  [15:0] D30,
  input  [15:0] D31,
  input  [4:0] s,
  output [15:0] y
);

  MUX_8_Bit_32x1 MUX_1 (
    .D0(D0[7:0]), .D1(D1[7:0]), .D2(D2[7:0]), .D3(D3[7:0]), .D4(D4[7:0]), .D5(D5[7:0]), .D6(D6[7:0]),
    .D7(D7[7:0]), .D8(D8[7:0]), .D9(D9[7:0]), .D10(D10[7:0]), .D11(D11[7:0]), .D12(D12[7:0]), .D13(D13[7:0]),
    .D14(D14[7:0]), .D15(D15[7:0]), .D16(D16[7:0]), .D17(D17[7:0]), .D18(D18[7:0]), .D19(D19[7:0]),
    .D20(D20[7:0]), .D21(D21[7:0]), .D22(D22[7:0]), .D23(D23[7:0]), .D24(D24[7:0]), .D25(D25[7:0]),
    .D26(D26[7:0]), .D27(D27[7:0]), .D28(D28[7:0]), .D29(D29[7:0]), .D30(D30[7:0]), .D31(D31[7:0]), .s(s),
    .y(y[7:0]));
  MUX_8_Bit_32x1 MUX_2 (
    .D0(D0[15:8]), .D1(D1[15:8]), .D2(D2[15:8]), .D3(D3[15:8]), .D4(D4[15:8]), .D5(D5[15:8]), .D6(D6[15:8]),
    .D7(D7[15:8]), .D8(D8[15:8]), .D9(D9[15:8]), .D10(D10[15:8]), .D11(D11[15:8]), .D12(D12[15:8]),
    .D13(D13[15:8]), .D14(D14[15:8]), .D15(D15[15:8]), .D16(D16[15:8]), .D17(D17[15:8]), .D18(D18[15:8]),
    .D19(D19[15:8]), .D20(D20[15:8]), .D21(D21[15:8]), .D22(D22[15:8]), .D23(D23[15:8]), .D24(D24[15:8]),
    .D25(D25[15:8]), .D26(D26[15:8]), .D27(D27[15:8]), .D28(D28[15:8]), .D29(D29[15:8]), .D30(D30[15:8]),
    .D31(D31[15:8]), .s(s), .y(y[15:8]));
endmodule

module MUX_32_Bit_32x1 (
  input  [31:0] D0,
  input  [31:0] D1,
  input  [31:0] D2,
  input  [31:0] D3,
  input  [31:0] D4,
  input  [31:0] D5,
  input  [31:0] D6,
  input  [31:0] D7,
  input  [31:0] D8,
  input  [31:0] D9,
  input  [31:0] D10,
  input  [31:0] D11,
  input  [31:0] D12,
  input  [31:0] D13,
  input  [31:0] D14,
  input  [31:0] D15,
  input  [31:0] D16,
  input  [31:0] D17,
  input  [31:0] D18,
  input  [31:0] D19,
  input  [31:0] D20,
  input  [31:0] D21,
  input  [31:0] D22,
  input  [31:0] D23,
  input  [31:0] D24,
  input  [31:0] D25,
  input  [31:0] D26,
  input  [31:0] D27,
  input  [31:0] D28,
  input  [31:0] D29,
  input  [31:0] D30,
  input  [31:0] D31,
  input  [4:0] s,
  output [31:0] y
);

  MUX_16_Bit_32x1 MUX_1 (
    .D0(D0[15:0]), .D1(D1[15:0]), .D2(D2[15:0]), .D3(D3[15:0]), .D4(D4[15:0]), .D5(D5[15:0]), .D6(D6[15:0]),
    .D7(D7[15:0]), .D8(D8[15:0]), .D9(D9[15:0]), .D10(D10[15:0]), .D11(D11[15:0]), .D12(D12[15:0]),
    .D13(D13[15:0]), .D14(D14[15:0]), .D15(D15[15:0]), .D16(D16[15:0]), .D17(D17[15:0]), .D18(D18[15:0]),
    .D19(D19[15:0]), .D20(D20[15:0]), .D21(D21[15:0]), .D22(D22[15:0]), .D23(D23[15:0]), .D24(D24[15:0]),
    .D25(D25[15:0]), .D26(D26[15:0]), .D27(D27[15:0]), .D28(D28[15:0]), .D29(D29[15:0]), .D30(D30[15:0]),
    .D31(D31[15:0]), .s(s), .y(y[15:0]));
  MUX_16_Bit_32x1 MUX_2 (
    .D0(D0[31:16]), .D1(D1[31:16]), .D2(D2[31:16]), .D3(D3[31:16]), .D4(D4[31:16]), .D5(D5[31:16]),
    .D6(D6[31:16]), .D7(D7[31:16]), .D8(D8[31:16]), .D9(D9[31:16]), .D10(D10[31:16]), .D11(D11[31:16]),
    .D12(D12[31:16]), .D13(D13[31:16]), .D14(D14[31:16]), .D15(D15[31:16]), .D16(D16[31:16]),
    .D17(D17[31:16]), .D18(D18[31:16]), .D19(D19[31:16]), .D20(D20[31:16]), .D21(D21[31:16]),
    .D22(D22[31:16]), .D23(D23[31:16]), .D24(D24[31:16]), .D25(D25[31:16]), .D26(D26[31:16]),
    .D27(D27[31:16]), .D28(D28[31:16]), .D29(D29[31:16]), .D30(D30[31:16]), .D31(D31[31:16]), .s(s),
    .y(y[31:16]));
endmodule

module Addierer_Subtrahierer_Komponente (
  input  A_S,
  input  UebetragIn,
  input  Summand1,
  input  Summand2,
  output Ergebnis,
  output UebertragOut
);

  wire and_1_out, and_2_out, xor_1_out, xor_2_out;

  xor xor_1 (xor_1_out, A_S, Summand2);
  xor xor_2 (xor_2_out, Summand1, xor_1_out);
  and and_1 (and_1_out, Summand1, xor_1_out);
  xor xor_3 (Ergebnis, xor_2_out, UebetragIn);
  and and_2 (and_2_out, xor_2_out, UebetragIn);
  or or_1 (UebertragOut, and_2_out, and_1_out);
endmodule

module Addierer_Subtrahierer_8_Bit (
  input  A_S,
  input  [7:0] In1,
  input  [7:0] In2,
  output [7:0] Summe,
  output Uebertrag
);

  wire addierer_subtrahierer_komponente_1_uebertragout, addierer_subtrahierer_komponente_2_uebertragout,
       addierer_subtrahierer_komponente_3_uebertragout, addierer_subtrahierer_komponente_4_uebertragout,
       addierer_subtrahierer_komponente_5_uebertragout, addierer_subtrahierer_komponente_6_uebertragout,
       addierer_subtrahierer_komponente_7_uebertragout, addierer_subtrahierer_komponente_8_uebertragout,
       not_1_out;

  not not_1 (not_1_out, A_S);
  Addierer_Subtrahierer_Komponente addierer_subtrahierer_komponente_1 (
    .A_S(A_S), .UebetragIn(A_S), .Summand1(In1[0]), .Summand2(In2[0]), .Ergebnis(Summe[0]),
    .UebertragOut(addierer_subtrahierer_komponente_1_uebertragout));
  Addierer_Subtrahierer_Komponente addierer_subtrahierer_komponente_2 (
    .A_S(A_S), .UebetragIn(addierer_subtrahierer_komponente_1_uebertragout), .Summand1(In1[1]),
    .Summand2(In2[1]), .Ergebnis(Summe[1]), .UebertragOut(addierer_subtrahierer_komponente_2_uebertragout));
  Addierer_Subtrahierer_Komponente addierer_subtrahierer_komponente_3 (
    .A_S(A_S), .UebetragIn(addierer_subtrahierer_komponente_2_uebertragout), .Summand1(In1[2]),
    .Summand2(In2[2]), .Ergebnis(Summe[2]), .UebertragOut(addierer_subtrahierer_komponente_3_uebertragout));
  Addierer_Subtrahierer_Komponente addierer_subtrahierer_komponente_4 (
    .A_S(A_S), .UebetragIn(addierer_subtrahierer_komponente_3_uebertragout), .Summand1(In1[3]),
    .Summand2(In2[3]), .Ergebnis(Summe[3]), .UebertragOut(addierer_subtrahierer_komponente_4_uebertragout));
  Addierer_Subtrahierer_Komponente addierer_subtrahierer_komponente_5 (
    .A_S(A_S), .UebetragIn(addierer_subtrahierer_komponente_4_uebertragout), .Summand1(In1[4]),
    .Summand2(In2[4]), .Ergebnis(Summe[4]), .UebertragOut(addierer_subtrahierer_komponente_5_uebertragout));
  Addierer_Subtrahierer_Komponente addierer_subtrahierer_komponente_6 (
    .A_S(A_S), .UebetragIn(addierer_subtrahierer_komponente_5_uebertragout), .Summand1(In1[5]),
    .Summand2(In2[5]), .Ergebnis(Summe[5]), .UebertragOut(addierer_subtrahierer_komponente_6_uebertragout));
  Addierer_Subtrahierer_Komponente addierer_subtrahierer_komponente_7 (
    .A_S(A_S), .UebetragIn(addierer_subtrahierer_komponente_6_uebertragout), .Summand1(In1[6]),
    .Summand2(In2[6]), .Ergebnis(Summe[6]), .UebertragOut(addierer_subtrahierer_komponente_7_uebertragout));
  Addierer_Subtrahierer_Komponente addierer_subtrahierer_komponente_8 (
    .A_S(A_S), .UebetragIn(addierer_subtrahierer_komponente_7_uebertragout), .Summand1(In1[7]),
    .Summand2(In2[7]), .Ergebnis(Summe[7]), .UebertragOut(addierer_subtrahierer_komponente_8_uebertragout));
  and and_1 (Uebertrag, addierer_subtrahierer_komponente_8_uebertragout, not_1_out);
endmodule

module AND_8_Bit (
  input  [7:0] Operand_1,
  input  [7:0] Operand_2,
  output [7:0] Ausgang
);

  and and_1 (Ausgang[0], Operand_1[0], Operand_2[0]);
  and and_2 (Ausgang[1], Operand_1[1], Operand_2[1]);
  and and_3 (Ausgang[2], Operand_1[2], Operand_2[2]);
  and and_4 (Ausgang[3], Operand_1[3], Operand_2[3]);
  and and_5 (Ausgang[4], Operand_1[4], Operand_2[4]);
  and and_6 (Ausgang[5], Operand_1[5], Operand_2[5]);
  and and_7 (Ausgang[6], Operand_1[6], Operand_2[6]);
  and and_8 (Ausgang[7], Operand_1[7], Operand_2[7]);
endmodule

module OR_8_Bit (
  input  [7:0] Operand1,
  input  [7:0] Operand2,
  output [7:0] Ausgang
);

  or or_1 (Ausgang[0], Operand1[0], Operand2[0]);
  or or_2 (Ausgang[1], Operand1[1], Operand2[1]);
  or or_3 (Ausgang[2], Operand1[2], Operand2[2]);
  or or_4 (Ausgang[3], Operand1[3], Operand2[3]);
  or or_5 (Ausgang[4], Operand1[4], Operand2[4]);
  or or_6 (Ausgang[5], Operand1[5], Operand2[5]);
  or or_7 (Ausgang[6], Operand1[6], Operand2[6]);
  or or_8 (Ausgang[7], Operand1[7], Operand2[7]);
endmodule

module XOR_8_Bit (
  input  [7:0] Operand1,
  input  [7:0] Operand2,
  output [7:0] Ausgang
);

  xor xor_1 (Ausgang[0], Operand1[0], Operand2[0]);
  xor xor_2 (Ausgang[1], Operand1[1], Operand2[1]);
  xor xor_3 (Ausgang[2], Operand1[2], Operand2[2]);
  xor xor_4 (Ausgang[3], Operand1[3], Operand2[3]);
  xor xor_5 (Ausgang[4], Operand1[4], Operand2[4]);
  xor xor_6 (Ausgang[5], Operand1[5], Operand2[5]);
  xor xor_7 (Ausgang[6], Operand1[6], Operand2[6]);
  xor xor_8 (Ausgang[7], Operand1[7], Operand2[7]);
endmodule

module XNOR_8_Bit (
  input  [7:0] Operand1,
  input  [7:0] Operand2,
  output [7:0] Ausgang
);

  xnor xnor_1 (Ausgang[0], Operand1[0], Operand2[0]);
  xnor xnor_2 (Ausgang[1], Operand1[1], Operand2[1]);
  xnor xnor_3 (Ausgang[2], Operand1[2], Operand2[2]);
  xnor xnor_4 (Ausgang[3], Operand1[3], Operand2[3]);
  xnor xnor_5 (Ausgang[4], Operand1[4], Operand2[4]);
  xnor xnor_6 (Ausgang[5], Operand1[5], Operand2[5]);
  xnor xnor_7 (Ausgang[6], Operand1[6], Operand2[6]);
  xnor xnor_8 (Ausgang[7], Operand1[7], Operand2[7]);
endmodule

module NAND_8_Bit (
  input  [7:0] Operand1,
  input  [7:0] Operand2,
  output [7:0] Ausgang
);

  nand nand_1 (Ausgang[0], Operand1[0], Operand2[0]);
  nand nand_2 (Ausgang[1], Operand1[1], Operand2[1]);
  nand nand_3 (Ausgang[2], Operand1[2], Operand2[2]);
  nand nand_4 (Ausgang[3], Operand1[3], Operand2[3]);
  nand nand_5 (Ausgang[4], Operand1[4], Operand2[4]);
  nand nand_6 (Ausgang[5], Operand1[5], Operand2[5]);
  nand nand_7 (Ausgang[6], Operand1[6], Operand2[6]);
  nand nand_8 (Ausgang[7], Operand1[7], Operand2[7]);
endmodule

module NOR_8_Bit (
  input  [7:0] Operand1,
  input  [7:0] Operand2,
  output [7:0] Ausgang
);

  nor nor_1 (Ausgang[0], Operand1[0], Operand2[0]);
  nor nor_2 (Ausgang[1], Operand1[1], Operand2[1]);
  nor nor_3 (Ausgang[2], Operand1[2], Operand2[2]);
  nor nor_4 (Ausgang[3], Operand1[3], Operand2[3]);
  nor nor_5 (Ausgang[4], Operand1[4], Operand2[4]);
  nor nor_6 (Ausgang[5], Operand1[5], Operand2[5]);
  nor nor_7 (Ausgang[6], Operand1[6], Operand2[6]);
  nor nor_8 (Ausgang[7], Operand1[7], Operand2[7]);
endmodule

module INV_8_Bit (
  input  [7:0] Operand,
  output [7:0] Ausgang
);

  not not_1 (Ausgang[0], Operand[0]);
  not not_2 (Ausgang[1], Operand[1]);
  not not_3 (Ausgang[2], Operand[2]);
  not not_4 (Ausgang[3], Operand[3]);
  not not_5 (Ausgang[4], Operand[4]);
  not not_6 (Ausgang[5], Operand[5]);
  not not_7 (Ausgang[6], Operand[6]);
  not not_8 (Ausgang[7], Operand[7]);
endmodule

module Multiplizierer_8_Bit (
  input  [7:0] Operant_2,
  input  [7:0] Operand_1,
  output [15:0] Ausgang
);

  wire [1:1] and_8x1_1_ausgang, and_8x1_2_ausgang, and_8x1_3_ausgang, and_8x1_4_ausgang, and_8x1_5_ausgang,
       and_8x1_6_ausgang, and_8x1_7_ausgang, and_8x1_8_ausgang;
  wire [7:0] and_8x1_1_ausgang_2, and_8x1_1_ausgang_3, and_8x1_1_ausgang_4, and_8x1_1_ausgang_5,
       and_8x1_1_ausgang_6, and_8x1_1_ausgang_7, and_8x1_2_ausgang_2;
  wire [7:1] addierer_8_bit_1_summe, addierer_8_bit_2_summe, addierer_8_bit_3_summe, addierer_8_bit_4_summe,
       addierer_8_bit_5_summe, addierer_8_bit_6_summe;
  wire [7:7] addierer_8_bit_1_uebertrag, addierer_8_bit_2_uebertrag, addierer_8_bit_3_uebertrag,
       addierer_8_bit_4_uebertrag, addierer_8_bit_5_uebertrag, addierer_8_bit_6_uebertrag;

  AND_8x1 and_8x1_1 (
    .Operand_1_8Bit(Operant_2), .Operand_2_1Bit(Operand_1[0]),
    .Ausgang({and_8x1_1_ausgang_7[0], and_8x1_1_ausgang_6[0], and_8x1_1_ausgang_5[0], and_8x1_1_ausgang_4[0], and_8x1_1_ausgang_3[0], and_8x1_1_ausgang_2[0], and_8x1_1_ausgang[1], Ausgang[0]}));
  AND_8x1 and_8x1_2 (
    .Operand_1_8Bit(Operant_2), .Operand_2_1Bit(Operand_1[1]),
    .Ausgang({and_8x1_1_ausgang_7[1], and_8x1_1_ausgang_6[1], and_8x1_1_ausgang_5[1], and_8x1_1_ausgang_4[1], and_8x1_1_ausgang_3[1], and_8x1_1_ausgang_2[1], and_8x1_2_ausgang[1], and_8x1_2_ausgang_2[0]}));
  AND_8x1 and_8x1_3 (
    .Operand_1_8Bit(Operant_2), .Operand_2_1Bit(Operand_1[2]),
    .Ausgang({and_8x1_1_ausgang_7[2], and_8x1_1_ausgang_6[2], and_8x1_1_ausgang_5[2], and_8x1_1_ausgang_4[2], and_8x1_1_ausgang_3[2], and_8x1_1_ausgang_2[2], and_8x1_3_ausgang[1], and_8x1_2_ausgang_2[1]}));
  AND_8x1 and_8x1_4 (
    .Operand_1_8Bit(Operant_2), .Operand_2_1Bit(Operand_1[3]),
    .Ausgang({and_8x1_1_ausgang_7[3], and_8x1_1_ausgang_6[3], and_8x1_1_ausgang_5[3], and_8x1_1_ausgang_4[3], and_8x1_1_ausgang_3[3], and_8x1_1_ausgang_2[3], and_8x1_4_ausgang[1], and_8x1_2_ausgang_2[2]}));
  AND_8x1 and_8x1_5 (
    .Operand_1_8Bit(Operant_2), .Operand_2_1Bit(Operand_1[4]),
    .Ausgang({and_8x1_1_ausgang_7[4], and_8x1_1_ausgang_6[4], and_8x1_1_ausgang_5[4], and_8x1_1_ausgang_4[4], and_8x1_1_ausgang_3[4], and_8x1_1_ausgang_2[4], and_8x1_5_ausgang[1], and_8x1_2_ausgang_2[3]}));
  AND_8x1 and_8x1_6 (
    .Operand_1_8Bit(Operant_2), .Operand_2_1Bit(Operand_1[5]),
    .Ausgang({and_8x1_1_ausgang_7[5], and_8x1_1_ausgang_6[5], and_8x1_1_ausgang_5[5], and_8x1_1_ausgang_4[5], and_8x1_1_ausgang_3[5], and_8x1_1_ausgang_2[5], and_8x1_6_ausgang[1], and_8x1_2_ausgang_2[4]}));
  AND_8x1 and_8x1_7 (
    .Operand_1_8Bit(Operant_2), .Operand_2_1Bit(Operand_1[6]),
    .Ausgang({and_8x1_1_ausgang_7[6], and_8x1_1_ausgang_6[6], and_8x1_1_ausgang_5[6], and_8x1_1_ausgang_4[6], and_8x1_1_ausgang_3[6], and_8x1_1_ausgang_2[6], and_8x1_7_ausgang[1], and_8x1_2_ausgang_2[5]}));
  AND_8x1 and_8x1_8 (
    .Operand_1_8Bit(Operant_2), .Operand_2_1Bit(Operand_1[7]),
    .Ausgang({and_8x1_1_ausgang_7[7], and_8x1_1_ausgang_6[7], and_8x1_1_ausgang_5[7], and_8x1_1_ausgang_4[7], and_8x1_1_ausgang_3[7], and_8x1_1_ausgang_2[7], and_8x1_8_ausgang[1], and_8x1_2_ausgang_2[6]}));
  Addierer_8_Bit addierer_8_bit_1 (
    .Summand_1({and_8x1_8_ausgang[1], and_8x1_7_ausgang[1], and_8x1_6_ausgang[1], and_8x1_5_ausgang[1], and_8x1_4_ausgang[1], and_8x1_3_ausgang[1], and_8x1_2_ausgang[1], and_8x1_1_ausgang[1]}),
    .Summand_2(and_8x1_2_ausgang_2), .Summe({addierer_8_bit_1_summe, Ausgang[1]}),
    .Uebertrag(addierer_8_bit_1_uebertrag[7]));
  Addierer_8_Bit addierer_8_bit_2 (
    .Summand_1({addierer_8_bit_1_uebertrag[7], addierer_8_bit_1_summe}), .Summand_2(and_8x1_1_ausgang_2),
    .Summe({addierer_8_bit_2_summe, Ausgang[2]}), .Uebertrag(addierer_8_bit_2_uebertrag[7]));
  Addierer_8_Bit addierer_8_bit_3 (
    .Summand_1({addierer_8_bit_2_uebertrag[7], addierer_8_bit_2_summe}), .Summand_2(and_8x1_1_ausgang_3),
    .Summe({addierer_8_bit_3_summe, Ausgang[3]}), .Uebertrag(addierer_8_bit_3_uebertrag[7]));
  Addierer_8_Bit addierer_8_bit_4 (
    .Summand_1({addierer_8_bit_3_uebertrag[7], addierer_8_bit_3_summe}), .Summand_2(and_8x1_1_ausgang_4),
    .Summe({addierer_8_bit_4_summe, Ausgang[4]}), .Uebertrag(addierer_8_bit_4_uebertrag[7]));
  Addierer_8_Bit addierer_8_bit_5 (
    .Summand_1({addierer_8_bit_4_uebertrag[7], addierer_8_bit_4_summe}), .Summand_2(and_8x1_1_ausgang_5),
    .Summe({addierer_8_bit_5_summe, Ausgang[5]}), .Uebertrag(addierer_8_bit_5_uebertrag[7]));
  Addierer_8_Bit addierer_8_bit_6 (
    .Summand_1({addierer_8_bit_5_uebertrag[7], addierer_8_bit_5_summe}), .Summand_2(and_8x1_1_ausgang_6),
    .Summe({addierer_8_bit_6_summe, Ausgang[6]}), .Uebertrag(addierer_8_bit_6_uebertrag[7]));
  Addierer_8_Bit addierer_8_bit_7 (
    .Summand_1({addierer_8_bit_6_uebertrag[7], addierer_8_bit_6_summe}), .Summand_2(and_8x1_1_ausgang_7),
    .Summe(Ausgang[14:7]), .Uebertrag(Ausgang[15]));
endmodule

module AND_8x1 (
  input  [7:0] Operand_1_8Bit,
  input  Operand_2_1Bit,
  output [7:0] Ausgang
);

  and and_1 (Ausgang[0], Operand_1_8Bit[0], Operand_2_1Bit);
  and and_2 (Ausgang[1], Operand_1_8Bit[1], Operand_2_1Bit);
  and and_3 (Ausgang[2], Operand_1_8Bit[2], Operand_2_1Bit);
  and and_4 (Ausgang[3], Operand_1_8Bit[3], Operand_2_1Bit);
  and and_5 (Ausgang[4], Operand_1_8Bit[4], Operand_2_1Bit);
  and and_6 (Ausgang[5], Operand_1_8Bit[5], Operand_2_1Bit);
  and and_7 (Ausgang[6], Operand_1_8Bit[6], Operand_2_1Bit);
  and and_8 (Ausgang[7], Operand_1_8Bit[7], Operand_2_1Bit);
endmodule

module Dividierer_8_Bit (
  input  [7:0] Dividend,
  input  [7:0] Divisor,
  input  Start_Load,
  input  CLK,
  input  Reset,
  output [7:0] out_6
);

  wire and_1_out, not_1_out, subtrahierer_8_bit_1_negativ;
  wire [4:0] subtrahierer_8_bit_2_negativ;
  wire [7:0] mux_8_bit_32x1_1_y, RegisterM_q, subtrahierer_8_bit_2_differenz, zaehler_4_bit_1_zahl;
  wire [7:1] RegisterA_q_2, undriven;
  wire [7:7] RegisterA_q;

  and and_1 (and_1_out, CLK, subtrahierer_8_bit_1_negativ);
  Zaehler_4_Bit zaehler_4_bit_1 (.Takt(CLK), .Reset(Reset), .Zahl(zaehler_4_bit_1_zahl));
  not not_1 (not_1_out, subtrahierer_8_bit_2_negativ[0]);
  Schieberegister_8_Bit RegisterQ (
    .Daten(Dividend), .D_SHL(not_1_out), .s({1'b1, Start_Load}), .Enable(1'b1), .CLK(and_1_out),
    .async_Reset(Reset), .Ausgang(out_6));  // open: D_SHR, sync_Reset
  Register_8_Bit RegisterA (
    .async_Reset(Start_Load), .LOAD(1'b1), .CLK(and_1_out), .D(mux_8_bit_32x1_1_y),
    .Q({RegisterA_q[7], RegisterA_q_2}));  // open: sync_reset, Nicht_Q
  Register_8_Bit RegisterM (
    .async_Reset(Reset), .LOAD(Start_Load), .CLK(and_1_out), .D(Divisor), .Q(RegisterM_q));  // open: sync_reset, Nicht_Q
  Subtrahierer_8_Bit subtrahierer_8_bit_1 (
    .Minuend(zaehler_4_bit_1_zahl), .Subtrahend({undriven[7:4], 1'b1, undriven[2:1], 1'b1}),
    .Negativ(subtrahierer_8_bit_1_negativ));  // open: Differenz
  Subtrahierer_8_Bit subtrahierer_8_bit_2 (
    .Minuend({RegisterA_q_2, out_6[7]}), .Subtrahend(RegisterM_q),
    .Differenz(subtrahierer_8_bit_2_differenz), .Negativ(subtrahierer_8_bit_2_negativ[0]));
  MUX_8_Bit_32x1 mux_8_bit_32x1_1 (
    .D0(subtrahierer_8_bit_2_differenz), .D1({RegisterA_q_2, out_6[7]}), .s(subtrahierer_8_bit_2_negativ),
    .y(mux_8_bit_32x1_1_y));  // open: D2, D3, D4, D5, D6, D7, D8, D9, D10, D11, D12, D13, D14, D15, D16, D17, D18, D19, D20, D21, D22, D23, D24, D25, D26, D27, D28, D29, D30, D31
endmodule

module Subtrahierer_8_Bit (
  input  [7:0] Minuend,
  input  [7:0] Subtrahend,
  output [7:0] Differenz,
  output Negativ
);

  wire addierer_subtrahierer_komponente_1_uebertragout, addierer_subtrahierer_komponente_2_uebertragout,
       addierer_subtrahierer_komponente_3_uebertragout, addierer_subtrahierer_komponente_4_uebertragout,
       addierer_subtrahierer_komponente_5_uebertragout, addierer_subtrahierer_komponente_6_uebertragout,
       addierer_subtrahierer_komponente_7_uebertragout, addierer_subtrahierer_komponente_8_uebertragout;

  Addierer_Subtrahierer_Komponente addierer_subtrahierer_komponente_1 (
    .A_S(1'b1), .UebetragIn(1'b1), .Summand1(Minuend[0]), .Summand2(Subtrahend[0]), .Ergebnis(Differenz[0]),
    .UebertragOut(addierer_subtrahierer_komponente_1_uebertragout));
  Addierer_Subtrahierer_Komponente addierer_subtrahierer_komponente_2 (
    .A_S(1'b1), .UebetragIn(addierer_subtrahierer_komponente_1_uebertragout), .Summand1(Minuend[1]),
    .Summand2(Subtrahend[1]), .Ergebnis(Differenz[1]),
    .UebertragOut(addierer_subtrahierer_komponente_2_uebertragout));
  Addierer_Subtrahierer_Komponente addierer_subtrahierer_komponente_3 (
    .A_S(1'b1), .UebetragIn(addierer_subtrahierer_komponente_2_uebertragout), .Summand1(Minuend[2]),
    .Summand2(Subtrahend[2]), .Ergebnis(Differenz[2]),
    .UebertragOut(addierer_subtrahierer_komponente_3_uebertragout));
  Addierer_Subtrahierer_Komponente addierer_subtrahierer_komponente_4 (
    .A_S(1'b1), .UebetragIn(addierer_subtrahierer_komponente_3_uebertragout), .Summand1(Minuend[3]),
    .Summand2(Subtrahend[3]), .Ergebnis(Differenz[3]),
    .UebertragOut(addierer_subtrahierer_komponente_4_uebertragout));
  Addierer_Subtrahierer_Komponente addierer_subtrahierer_komponente_5 (
    .A_S(1'b1), .UebetragIn(addierer_subtrahierer_komponente_4_uebertragout), .Summand1(Minuend[4]),
    .Summand2(Subtrahend[4]), .Ergebnis(Differenz[4]),
    .UebertragOut(addierer_subtrahierer_komponente_5_uebertragout));
  Addierer_Subtrahierer_Komponente addierer_subtrahierer_komponente_6 (
    .A_S(1'b1), .UebetragIn(addierer_subtrahierer_komponente_5_uebertragout), .Summand1(Minuend[5]),
    .Summand2(Subtrahend[5]), .Ergebnis(Differenz[5]),
    .UebertragOut(addierer_subtrahierer_komponente_6_uebertragout));
  Addierer_Subtrahierer_Komponente addierer_subtrahierer_komponente_7 (
    .A_S(1'b1), .UebetragIn(addierer_subtrahierer_komponente_6_uebertragout), .Summand1(Minuend[6]),
    .Summand2(Subtrahend[6]), .Ergebnis(Differenz[6]),
    .UebertragOut(addierer_subtrahierer_komponente_7_uebertragout));
  Addierer_Subtrahierer_Komponente addierer_subtrahierer_komponente_8 (
    .A_S(1'b1), .UebetragIn(addierer_subtrahierer_komponente_7_uebertragout), .Summand1(Minuend[7]),
    .Summand2(Subtrahend[7]), .Ergebnis(Differenz[7]),
    .UebertragOut(addierer_subtrahierer_komponente_8_uebertragout));
  not not_1 (Negativ, addierer_subtrahierer_komponente_8_uebertragout);
endmodule

module Zaehler_4_Bit (
  input  Takt,
  input  Reset,
  output [7:0] Zahl
);

  wire and_1_out, and_2_out, and_3_out, not_1_out, xor_1_out, xor_2_out, xor_3_out, xor_4_out;

  not not_1 (not_1_out, Takt);
  and and_1 (and_1_out, Takt, Zahl[0]);
  and and_2 (and_2_out, and_1_out, Zahl[1]);
  and and_3 (and_3_out, and_2_out, Zahl[2]);
  xor xor_1 (xor_1_out, Takt, Zahl[0]);
  xor xor_2 (xor_2_out, and_1_out, Zahl[1]);
  xor xor_3 (xor_3_out, and_2_out, Zahl[2]);
  xor xor_4 (xor_4_out, and_3_out, Zahl[3]);
  D_Flipflop d_flipflop_1 (
    .D(xor_1_out), .CLK(not_1_out), .async_Reset(Reset), .Q(Zahl[0]));  // open: sync_Reset, not_Q
  D_Flipflop d_flipflop_2 (
    .D(xor_2_out), .CLK(not_1_out), .async_Reset(Reset), .Q(Zahl[1]));  // open: sync_Reset, not_Q
  D_Flipflop d_flipflop_3 (
    .D(xor_3_out), .CLK(not_1_out), .async_Reset(Reset), .Q(Zahl[2]));  // open: sync_Reset, not_Q
  D_Flipflop d_flipflop_4 (
    .D(xor_4_out), .CLK(not_1_out), .async_Reset(Reset), .Q(Zahl[3]));  // open: sync_Reset, not_Q
endmodule

module Speicher (
  input  [3:0] Adresse,
  input  [7:0] Daten_Eingang,
  input  async_Reset,
  input  sync_Reset,
  input  CLK,
  output [7:0] Daten_Ausgang
);

  wire [7:0] register_8_bit_1_q, register_8_bit_2_q, register_8_bit_3_q, register_8_bit_4_q,
       register_8_bit_5_q, register_8_bit_6_q, register_8_bit_7_q, register_8_bit_8_q, register_8_bit_9_q,
       register_8_bit_10_q, register_8_bit_11_q, register_8_bit_12_q, register_8_bit_13_q,
       register_8_bit_14_q, register_8_bit_15_q, register_8_bit_16_q;

  Register_8_Bit register_8_bit_1 (
    .D(Daten_Eingang), .Q(register_8_bit_1_q));  // open: async_Reset, sync_reset, LOAD, CLK, Nicht_Q
  Register_8_Bit register_8_bit_2 (
    .D(Daten_Eingang), .Q(register_8_bit_2_q));  // open: async_Reset, sync_reset, LOAD, CLK, Nicht_Q
  Register_8_Bit register_8_bit_3 (
    .D(Daten_Eingang), .Q(register_8_bit_3_q));  // open: async_Reset, sync_reset, LOAD, CLK, Nicht_Q
  Register_8_Bit register_8_bit_4 (
    .D(Daten_Eingang), .Q(register_8_bit_4_q));  // open: async_Reset, sync_reset, LOAD, CLK, Nicht_Q
  Register_8_Bit register_8_bit_5 (
    .D(Daten_Eingang), .Q(register_8_bit_5_q));  // open: async_Reset, sync_reset, LOAD, CLK, Nicht_Q
  Register_8_Bit register_8_bit_6 (
    .D(Daten_Eingang), .Q(register_8_bit_6_q));  // open: async_Reset, sync_reset, LOAD, CLK, Nicht_Q
  Register_8_Bit register_8_bit_7 (
    .D(Daten_Eingang), .Q(register_8_bit_7_q));  // open: async_Reset, sync_reset, LOAD, CLK, Nicht_Q
  Register_8_Bit register_8_bit_8 (
    .D(Daten_Eingang), .Q(register_8_bit_8_q));  // open: async_Reset, sync_reset, LOAD, CLK, Nicht_Q
  Register_8_Bit register_8_bit_9 (
    .D(Daten_Eingang), .Q(register_8_bit_9_q));  // open: async_Reset, sync_reset, LOAD, CLK, Nicht_Q
  Register_8_Bit register_8_bit_10 (
    .D(Daten_Eingang), .Q(register_8_bit_10_q));  // open: async_Reset, sync_reset, LOAD, CLK, Nicht_Q
  Register_8_Bit register_8_bit_11 (
    .D(Daten_Eingang), .Q(register_8_bit_11_q));  // open: async_Reset, sync_reset, LOAD, CLK, Nicht_Q
  Register_8_Bit register_8_bit_12 (
    .D(Daten_Eingang), .Q(register_8_bit_12_q));  // open: async_Reset, sync_reset, LOAD, CLK, Nicht_Q
  Register_8_Bit register_8_bit_13 (
    .D(Daten_Eingang), .Q(register_8_bit_13_q));  // open: async_Reset, sync_reset, LOAD, CLK, Nicht_Q
  Register_8_Bit register_8_bit_14 (
    .D(Daten_Eingang), .Q(register_8_bit_14_q));  // open: async_Reset, sync_reset, LOAD, CLK, Nicht_Q
  Register_8_Bit register_8_bit_15 (
    .D(Daten_Eingang), .Q(register_8_bit_15_q));  // open: async_Reset, sync_reset, LOAD, CLK, Nicht_Q
  Register_8_Bit register_8_bit_16 (
    .D(Daten_Eingang), .Q(register_8_bit_16_q));  // open: async_Reset, sync_reset, LOAD, CLK, Nicht_Q
  MUX_8_Bit_16x1 mux_8_bit_16x1_1 (
    .D0(register_8_bit_1_q), .D1(register_8_bit_2_q), .D2(register_8_bit_3_q), .D3(register_8_bit_4_q),
    .D4(register_8_bit_5_q), .D5(register_8_bit_6_q), .D6(register_8_bit_7_q), .D7(register_8_bit_8_q),
    .D8(register_8_bit_9_q), .D9(register_8_bit_10_q), .D10(register_8_bit_11_q), .D11(register_8_bit_12_q),
    .D12(register_8_bit_13_q), .D13(register_8_bit_14_q), .D14(register_8_bit_15_q),
    .D15(register_8_bit_16_q), .s(Adresse), .y(Daten_Ausgang));

  // Notes on the sheet:
  //   Speicher ist noch nicht fertig implementiert
endmodule
